// Logisim project CPU.circ as structural Verilog: 5 circuits, main circuit computer
module alu8 (
  input  rsl,
  input  lsr,
  input  \xor ,
  input  \or ,
  input  \and ,
  input  add,
  input  sub,
  input  [7:0] b,
  input  [7:0] a,
  output [7:0] x,
  output out_11,
  output out_12,
  output out_13
);

  wire adder_1_cout, leftshift8_1_out_3, or_2_out, rightshift8_1_out_2;
  wire [7:0] adder_1_out, and_1_out, bit_extender_1_out, leftshift8_1_out_2, or_1_out, rightshift8_1_out_3,
       xor_1_out, xor_2_out;

  assign bit_extender_1_out = {{7{sub}}, sub};  // Bit_Extender bit_extender_1
  assign xor_1_out = bit_extender_1_out ^ b;  // XOR_Gate xor_1, 8 bits wide
  Adder adder_1 (.a(xor_1_out), .b(a), .out(adder_1_out), .cin(sub), .cout(adder_1_cout));
  assign and_1_out = b & a;  // AND_Gate and_1, 8 bits wide
  assign or_1_out = b | a;  // OR_Gate or_1, 8 bits wide
  assign xor_2_out = b ^ a;  // XOR_Gate xor_2, 8 bits wide
  leftshift8 leftshift8_1 (.in_1(a), .out_2(leftshift8_1_out_2), .out_3(leftshift8_1_out_3));
  rightshift8 rightshift8_1 (.in_1(a), .out_3(rightshift8_1_out_3), .out_2(rightshift8_1_out_2));
  or or_2 (or_2_out, add, sub);
  assign out_11 = or_2_out ? adder_1_cout : 1'bz;  // Controlled_Buffer controlled_buffer_1
  assign out_11 = lsr ? leftshift8_1_out_3 : 1'bz;  // Controlled_Buffer controlled_buffer_2
  assign out_11 = rsl ? rightshift8_1_out_2 : 1'bz;  // Controlled_Buffer controlled_buffer_3
  assign {out_13, x[6:0]} = or_2_out ? adder_1_out : 8'bz;  // Controlled_Buffer controlled_buffer_4
  assign {out_13, x[6:0]} = \and  ? and_1_out : 8'bz;  // Controlled_Buffer controlled_buffer_5
  assign {out_13, x[6:0]} = \or  ? or_1_out : 8'bz;  // Controlled_Buffer controlled_buffer_6
  assign {out_13, x[6:0]} = \xor  ? xor_2_out : 8'bz;  // Controlled_Buffer controlled_buffer_7
  assign {out_13, x[6:0]} = lsr ? leftshift8_1_out_2 : 8'bz;  // Controlled_Buffer controlled_buffer_8
  assign {out_13, x[6:0]} = rsl ? rightshift8_1_out_3 : 8'bz;  // Controlled_Buffer controlled_buffer_9
  nor nor_1 (out_12, x[0], x[1], x[2], x[3], x[5], x[6], out_13, x[4]);

  assign x[7] = out_13;
endmodule

module leftshift8 (
  input  [7:0] in_1,
  output [7:0] out_2,
  output out_3
);


  assign out_2 = {in_1[6:0], 1'b0};
  assign out_3 = in_1[7];
endmodule

module rightshift8 (
  input  [7:0] in_1,
  output out_2,
  output [7:0] out_3
);


  assign out_2 = in_1[0];
  assign out_3 = {1'b0, in_1[7:1]};
endmodule

module computer (
);

  wire alu8_1_out_11, alu8_1_out_12, alu8_1_out_13, and_1_out, and_2_out, and_3_out, and_4_out, and_5_out,
       and_6_out, and_7_out, and_8_out, and_9_out, and_10_out, and_11_out, and_12_out, and_13_out,
       and_14_out, and_15_out, and_16_out, and_17_out, and_18_out, and_19_out, and_20_out, and_21_out,
       and_22_out, and_23_out, and_24_out, and_25_out, buffer_1_out, button_1_out, clock_1_out,
       controlled_buffer_3_out, d_ff_1_q, d_ff_2_q, d_ff_4_q, decoder_1_out0, decoder_1_out1, decoder_1_out2,
       decoder_1_out3, decoder_1_out4, decoder_1_out5, decoder_1_out6, not_1_out, or_1_out, xnor_1_out,
       xnor_2_out, xnor_3_out, xor_1_out, xor_2_out;
  wire [0:0] not_2_out, not_3_out, not_4_out, not_5_out, not_7_out, register_3_q_2;
  wire [2:0] controlled_buffer_1_out_2, controlled_buffer_1_out_3, controlled_buffer_1_out_4, d_ff_3_q;
  wire [7:0] alu8_1_x, controlled_buffer_10_out, counter_1_q, multiplexer_1_out, multiplexer_2_out,
       multiplexer_3_out, register_1_q, register_2_q;
  wire [7:2] register_3_q_3;
  wire [16:15] or_2_out;
  wire [17:17] register_3_q;
  wire [20:0] controlled_buffer_1_out;

  Clock clock_1 (.out(clock_1_out));
  Button button_1 (.out(button_1_out));
  D_Flip_Flop #(.trigger("falling")) d_ff_1 (
    .clk(button_1_out), .D(clock_1_out), .Q(d_ff_1_q));  // open: Qn, preset, en, reset
  xnor xnor_1 (xnor_1_out, d_ff_1_q, clock_1_out);
  Register register_1 (
    .D(alu8_1_x), .en(controlled_buffer_1_out[0]), .Q(register_1_q), .clk(xnor_1_out), .clr(button_1_out));
  Register register_2 (
    .D(alu8_1_x), .en(controlled_buffer_1_out[1]), .Q(register_2_q), .clk(xnor_1_out), .clr(button_1_out));
  // Probe on {controlled_buffer_1_out[20], controlled_buffer_1_out_4, controlled_buffer_1_out[16:14], controlled_buffer_1_out_3, controlled_buffer_1_out_2, controlled_buffer_1_out[7:0]}
  Multiplexer #(.select(3), .width(8), .enable("false")) multiplexer_1 (
    .in0(register_1_q), .in1(register_2_q), .in2(controlled_buffer_10_out), .out(multiplexer_1_out),
    .sel(controlled_buffer_1_out[7:5]));  // open: in3, in4, in5, in6, in7
  Multiplexer #(.select(3), .width(8), .enable("false")) multiplexer_2 (
    .in0(register_1_q), .in1(register_2_q), .in2({8{1'b0}}), .in3(controlled_buffer_10_out),
    .out(multiplexer_2_out), .sel(controlled_buffer_1_out[4:2]));  // open: in4, in5, in6, in7
  and and_1 (and_1_out, xnor_1_out, d_ff_2_q);
  assign {controlled_buffer_1_out[20], controlled_buffer_1_out_4, controlled_buffer_1_out[16:14], controlled_buffer_1_out_3, controlled_buffer_1_out_2, controlled_buffer_1_out[7:0]} = and_1_out ? 21'h150000 : 21'bz;  // Controlled_Buffer controlled_buffer_1
  D_Flip_Flop d_ff_2 (
    .clk(xnor_1_out), .D(controlled_buffer_3_out), .Q(d_ff_2_q), .preset(button_1_out));  // open: Qn, en, reset
  not not_1 (not_1_out, and_1_out);
  and and_2 (and_2_out, and_3_out, ~xnor_2_out);  // AND_Gate
  assign {controlled_buffer_1_out[20], controlled_buffer_1_out_4, controlled_buffer_1_out[16:14], controlled_buffer_1_out_3, controlled_buffer_1_out_2, controlled_buffer_1_out[7:0]} = and_2_out ? {15'h5404, register_3_q_2[0], 3'b010, register_3_q[17], not_2_out[0]} : 21'bz;  // Controlled_Buffer controlled_buffer_2
  and and_3 (and_3_out, and_8_out, not_1_out);
  assign controlled_buffer_3_out = and_2_out ? 1'b1 : 1'bz;  // Controlled_Buffer controlled_buffer_3
  and and_4 (and_4_out, and_9_out, not_1_out);
  and and_5 (and_5_out, and_10_out, not_1_out);
  not not_2 (not_2_out[0], register_3_q[17]);
  assign {controlled_buffer_1_out[20], controlled_buffer_1_out_4, controlled_buffer_1_out[16:14], controlled_buffer_1_out_3, controlled_buffer_1_out_2, controlled_buffer_1_out[7:0]} = and_4_out ? {3'b000, register_3_q[17], 11'h104, register_3_q_2[0], 5'b01000} : 21'bz;  // Controlled_Buffer controlled_buffer_4
  not not_3 (not_3_out[0], register_3_q[17]);
  assign {controlled_buffer_1_out[20], controlled_buffer_1_out_4, controlled_buffer_1_out[16:14], controlled_buffer_1_out_3, controlled_buffer_1_out_2, controlled_buffer_1_out[7:0]} = and_5_out ? {3'b100, register_3_q_2[0], 15'h52, register_3_q[17], not_3_out[0]} : 21'bz;  // Controlled_Buffer controlled_buffer_5
  // Probe on multiplexer_1_out
  // Probe on multiplexer_2_out
  assign controlled_buffer_3_out = and_4_out ? 1'b1 : 1'bz;  // Controlled_Buffer controlled_buffer_6
  assign controlled_buffer_3_out = and_5_out ? 1'b1 : 1'bz;  // Controlled_Buffer controlled_buffer_7
  Decoder #(.select(3), .enable("false")) decoder_1 (
    .out0(decoder_1_out0), .out1(decoder_1_out1), .out2(decoder_1_out2), .out3(decoder_1_out3),
    .out4(decoder_1_out4), .out5(decoder_1_out5), .out6(decoder_1_out6), .sel(controlled_buffer_1_out_2));  // open: out7
  xor xor_1 (xor_1_out, xnor_1_out, buffer_1_out);
  buf buffer_1 (buffer_1_out, xnor_1_out);
  and and_6 (and_6_out, d_ff_2_q, ~controlled_buffer_3_out);  // AND_Gate
  xnor xnor_2 (xnor_2_out, register_3_q[17], register_3_q_2[0]);
  and and_7 (and_7_out, and_3_out, xnor_2_out);
  assign {controlled_buffer_1_out[20], controlled_buffer_1_out_4, controlled_buffer_1_out[16:14], controlled_buffer_1_out_3, controlled_buffer_1_out_2, controlled_buffer_1_out[7:0]} = and_7_out ? {19'h54052, register_3_q[17], not_4_out[0]} : 21'bz;  // Controlled_Buffer controlled_buffer_8
  Counter counter_1 (
    .load(controlled_buffer_1_out[15]), .D(alu8_1_x), .count(controlled_buffer_1_out[16]), .Q(counter_1_q),
    .clk(xor_1_out), .clr(button_1_out));  // open: carry
  assign controlled_buffer_3_out = and_7_out ? 1'b1 : 1'bz;  // Controlled_Buffer controlled_buffer_9
  alu8 alu8_1 (
    .rsl(decoder_1_out6), .lsr(decoder_1_out5), .\xor (decoder_1_out4), .\or (decoder_1_out3),
    .\and (decoder_1_out2), .add(decoder_1_out1), .sub(decoder_1_out0), .b(multiplexer_2_out),
    .a(multiplexer_1_out), .x(alu8_1_x), .out_11(alu8_1_out_11), .out_12(alu8_1_out_12),
    .out_13(alu8_1_out_13));
  // Probe on controlled_buffer_1_out_4
  not not_4 (not_4_out[0], register_3_q[17]);
  D_Flip_Flop d_ff_3 (
    .clk(xnor_1_out), .D(alu8_1_out_12), .Q(d_ff_3_q[0]), .en(controlled_buffer_1_out_3[2]),
    .reset(button_1_out));  // open: Qn, preset
  Multiplexer #(.select(3), .width(8), .enable("false")) multiplexer_3 (
    .in0(register_1_q), .in1(register_2_q), .in2(counter_1_q), .out(multiplexer_3_out),
    .sel(controlled_buffer_1_out_4));  // open: in3, in4, in5, in6, in7
  D_Flip_Flop d_ff_4 (.clk(xnor_1_out), .D(and_6_out), .Q(d_ff_4_q), .reset(button_1_out));  // open: Qn, preset, en
  // Probe on alu8_1_x
  D_Flip_Flop d_ff_5 (
    .clk(xnor_1_out), .D(alu8_1_out_11), .Q(d_ff_3_q[1]), .en(controlled_buffer_1_out_3[1]),
    .reset(button_1_out));  // open: Qn, preset
  assign controlled_buffer_10_out = controlled_buffer_1_out[14] ? alu8_1_x : 8'bz;  // Controlled_Buffer controlled_buffer_10
  D_Flip_Flop d_ff_6 (
    .clk(xnor_1_out), .D(alu8_1_out_13), .Q(d_ff_3_q[2]), .en(controlled_buffer_1_out_3[0]),
    .reset(button_1_out));  // open: Qn, preset
  RAM ram_1 (
    .addr(multiplexer_3_out), .data(controlled_buffer_10_out), .sel(1'b1), .clk(xnor_1_out),
    .ld(controlled_buffer_1_out[20]));  // open: clr
  Register #(.trigger("falling")) register_3 (
    .D(controlled_buffer_10_out), .en(d_ff_2_q), .Q({register_3_q_3, register_3_q[17], register_3_q_2[0]}),
    .clk(xnor_1_out), .clr(button_1_out));
  and and_8 (and_8_out, ~register_3_q_3[2], ~register_3_q_3[3], ~register_3_q_3[4], ~register_3_q_3[5], ~register_3_q_3[6], ~register_3_q_3[7]);  // AND_Gate
  and and_9 (and_9_out, ~register_3_q_3[2], register_3_q_3[3], ~register_3_q_3[4], ~register_3_q_3[5], ~register_3_q_3[6], ~register_3_q_3[7]);  // AND_Gate
  and and_10 (and_10_out, register_3_q_3[2], ~register_3_q_3[3], ~register_3_q_3[4], ~register_3_q_3[5], ~register_3_q_3[6], ~register_3_q_3[7]);  // AND_Gate
  and and_11 (and_11_out, and_25_out, not_1_out);
  and and_12 (and_12_out, and_23_out, not_1_out);
  and and_13 (and_13_out, and_24_out, not_1_out);
  assign controlled_buffer_3_out = and_11_out ? 1'b1 : 1'bz;  // Controlled_Buffer controlled_buffer_11
  assign controlled_buffer_3_out = and_12_out ? 1'b1 : 1'bz;  // Controlled_Buffer controlled_buffer_12
  and and_14 (and_14_out, and_13_out, ~xnor_3_out);  // AND_Gate
  assign {controlled_buffer_1_out[20], controlled_buffer_1_out_4, controlled_buffer_1_out[16:14], controlled_buffer_1_out_3, controlled_buffer_1_out_2, controlled_buffer_1_out[7:0]} = and_14_out ? {12'ha1c, register_3_q_3[3], 2'b00, register_3_q[17], 2'b00, register_3_q_2[0], register_3_q[17], not_5_out[0]} : 21'bz;  // Controlled_Buffer controlled_buffer_13
  assign {controlled_buffer_1_out[20], controlled_buffer_1_out_4, controlled_buffer_1_out[16:14], controlled_buffer_1_out_3, controlled_buffer_1_out_2, controlled_buffer_1_out[7:0]} = and_11_out ? 21'h140000 : 21'bz;  // Controlled_Buffer controlled_buffer_14
  assign {controlled_buffer_1_out[20], controlled_buffer_1_out_4, controlled_buffer_1_out[16:14], controlled_buffer_1_out_3, controlled_buffer_1_out_2, controlled_buffer_1_out[7:0]} = and_12_out ? {4'b1010, or_2_out, 15'h148} : 21'bz;  // Controlled_Buffer controlled_buffer_15
  not not_5 (not_5_out[0], register_3_q[17]);
  assign controlled_buffer_3_out = and_13_out ? 1'b1 : 1'bz;  // Controlled_Buffer controlled_buffer_16
  and and_15 (and_15_out, register_3_q[17], ~register_3_q_2[0]);  // AND_Gate
  and and_16 (and_16_out, d_ff_3_q[1], ~d_ff_3_q[0], and_18_out);  // AND_Gate
  and and_17 (and_17_out, ~d_ff_3_q[1], and_15_out);  // AND_Gate
  or or_1 (or_1_out, and_17_out, and_16_out, and_20_out);
  xor xor_2 (xor_2_out, register_3_q_3[2], or_1_out);
  or or_2 (or_2_out[15], xor_2_out, and_21_out);
  not not_6 (or_2_out[16], or_2_out[15]);
  and and_18 (and_18_out, ~register_3_q[17], register_3_q_2[0]);  // AND_Gate
  and and_19 (and_19_out, ~register_3_q[17], ~register_3_q_2[0]);  // AND_Gate
  and and_20 (and_20_out, d_ff_3_q[0], and_19_out);
  and and_21 (and_21_out, ~register_3_q_3[2], register_3_q[17], register_3_q_2[0]);  // AND_Gate
  xnor xnor_3 (xnor_3_out, register_3_q[17], register_3_q_2[0]);
  and and_22 (and_22_out, xnor_3_out, and_13_out);
  assign {controlled_buffer_1_out[20], controlled_buffer_1_out_4, controlled_buffer_1_out[16:14], controlled_buffer_1_out_3, controlled_buffer_1_out_2, controlled_buffer_1_out[7:0]} = and_22_out ? {12'ha9c, register_3_q_3[3], 2'b00, register_3_q[17], 3'b011, register_3_q[17], not_7_out[0]} : 21'bz;  // Controlled_Buffer controlled_buffer_17
  not not_7 (not_7_out[0], register_3_q[17]);
  and and_23 (and_23_out, ~register_3_q_3[3], ~register_3_q_3[4], register_3_q_3[5], ~register_3_q_3[6], ~register_3_q_3[7]);  // AND_Gate
  and and_24 (and_24_out, register_3_q_3[4], ~register_3_q_3[5], ~register_3_q_3[6], ~register_3_q_3[7]);  // AND_Gate
  and and_25 (and_25_out, ~register_3_q_2[0], ~register_3_q[17], ~register_3_q_3[2], register_3_q_3[3], ~register_3_q_3[4], register_3_q_3[5], ~register_3_q_3[6], ~register_3_q_3[7]);  // AND_Gate

  // Notes on the sheet:
  //   clr
  //   clk
  //   a
  //   b
  //   clk
  //   ALU ctrl
  //   phase reset
  //   phase 1
  //   F-bus
  //   mov r,r / mov r,imm
  //   mov [r],r
  //   mov r,[r]
  //   Chili Pork Unit
  //   ip
  //   A-sel
  //   z
  //   phase 2
  //   c
  //   A-Bus
  //   s
  //   D-bus
  //   add/sub r,r
  //   nop
  //   jb
  //   je
  //   ja
  //   jmp
  //   add/sub r,imm
endmodule

module cock (
  input  in_1
);

  wire buffer_1_out, button_1_out, xor_1_out;

  xor xor_1 (xor_1_out, in_1, buffer_1_out);
  buf buffer_1 (buffer_1_out, in_1);
  Button button_1 (.out(button_1_out));
  Counter counter_1 (.count(1'b1), .clk(xor_1_out), .clr(button_1_out));  // open: load, D, Q, carry
endmodule
